# Fritzing sketch montage_final (saved by Fritzing 0.9.3b)
breadboards: 1

parts:
  Raspberry_Pi_1 = Raspberry Pi 3 [part_number=RPI-3-V1.2]  # not connected
  LCD2 = LCD screen
  LCM1602_IIC2 = LCM1602 IIC [part_number="LCM1602 IIC" chip_label="LCM1602 IIC" package="DIP (Dual Inline) [THT]"]
  Composant1 = Adafruit T-Cobbler Plus [part_number="Adafruit #1989 and #2028"]
  Keypad4x1 = Keypad Membran 4x4
  125_kHz_RFID_module1 = RDM6300
  Part4 = RDM6300-ANT
  R1 = Resistor [tolerance=±5% resistance=220 package="2512 [SMD]"]
  R2 = Resistor [tolerance=±5% resistance=220 package="0603 [SMD]"]
  J1 = Basic Servo

nets:
  VSS: LCD2.VSS, LCM1602_IIC2.VSS
  VDD: LCD2.VDD, LCM1602_IIC2.VDD
  N1: LCD2.V0, LCM1602_IIC2.V0
  N2: LCD2.RS, LCM1602_IIC2.RS
  N3: LCD2.R/W, LCM1602_IIC2.RW
  N4: LCD2.E, LCM1602_IIC2.E
  N5: LCD2.DB0, LCM1602_IIC2.D0
  N6: LCD2.DB1, LCM1602_IIC2.D1
  N7: LCD2.DB2, LCM1602_IIC2.D2
  N8: LCD2.DB3, LCM1602_IIC2.D3
  N9: LCD2.DB4, LCM1602_IIC2.D4
  N10: LCD2.DB5, LCM1602_IIC2.D5
  N11: LCD2.DB6, LCM1602_IIC2.D6
  N12: LCD2.DB7, LCM1602_IIC2.D7
  N13: LCD2.LED+, LCM1602_IIC2.A
  N14: LCD2.LED-, LCM1602_IIC2.K
  GND: LCM1602_IIC2.GND, Composant1.GND, 125_kHz_RFID_module1.GND, J1.gnd
  N15: LCM1602_IIC2.SDA, Composant1.SDA
  N16: LCM1602_IIC2.SCL, Composant1.SCL
  N17: LCM1602_IIC2.LED_A, LCM1602_IIC2.LED_B
  N18: Composant1.GPIO5, Keypad4x1.Pin1
  N19: Composant1.GPIO6, Keypad4x1.Pin2
  N20: Composant1.GPIO13, Keypad4x1.Pin3
  N21: Composant1.GPIO19, Keypad4x1.Pin4
  +5V: Composant1.+5V, 125_kHz_RFID_module1.+5V, J1.vcc
  N22: Composant1.RXD, R1.Pin_0, R2.Pin_1
  N23: Composant1.GPIO18, J1.pulse
  N24: Composant1.GPIO12, Keypad4x1.Pin5
  N25: Composant1.GPIO16, Keypad4x1.Pin6
  N26: Composant1.GPIO20, Keypad4x1.Pin7
  N27: Composant1.GPIO21, Keypad4x1.Pin8
  N28: 125_kHz_RFID_module1.ANT1, Part4.ANT1
  N29: 125_kHz_RFID_module1.ANT2, Part4.ANT2

custom parts:
  LCM1602 IIC: I2C-Module to use a 1602 or 2004 LCD on with the wire.h libory Serial LCD Modul
  Adafruit T-Cobbler Plus: The Raspberry Pi has landed on the Maker World like a 40-GPIO pinned, quad-USB ported, credit card sized bomb of DIY joy. And while you can use most of our great Model B accessories by hooking up our downgrade cable, its probably a good time to upgrade your set up and accessorize using all of the 40 pins. That's why we now carry the Assembled Adafruit Pi T-Cobbler Plus - Breakout + Cable for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
  Keypad Membran 4x4: Membrane Keypad 4x4 Matrix
  RDM6300: 125 kHz RFID module (serial interface)
  RDM6300-ANT: Antenna
